# Fritzing sketch 6DOF (saved by Fritzing 0.9.2b)
breadboards: 1

parts:
  S2 = Round Pushbutton  # not connected
  Teensy_3_1 = Teensy 3.1
  Part1 = IMU Digital Combo Board 6DOF

nets:
  GND: Teensy_3_1.GND, Part1.GND
  N1: Teensy_3_1.A4/D18, Part1.SDA
  N2: Teensy_3_1.A5/D19, Part1.SCL
  3V3: Teensy_3_1.3V3, Part1.3.3V

notes:
  GND
  3.3V
  6DOF
