# Fritzing sketch contact (saved by Fritzing 0.9.2b)
breadboards: 1

parts:
  S2 = Round Pushbutton  # not connected
  Teensy_3_1 = Teensy 3.1
  U1 = BUTTON-MAGNETIC [package=Magnetic-snap]
  U2 = BUTTON-MAGNETIC [package=Magnetic-snap]
  U3 = BUTTON-MAGNETIC [package=Magnetic-snap]
  U4 = BUTTON-MAGNETIC [package=Magnetic-snap]
  U5 = BUTTON-MAGNETIC [package=Magnetic-snap]
  U6 = BUTTON-MAGNETIC [package=Magnetic-snap]
  U7 = BUTTON-MAGNETIC [package=Magnetic-snap]

nets:
  N1: Teensy_3_1.GND, U5.1, U6.1, U7.1
  N2: Teensy_3_1.D2, U1.1
  N3: Teensy_3_1.D3, U2.1
  N4: Teensy_3_1.D4, U3.1
  N5: Teensy_3_1.D5, U4.1

notes:
  GND
  Common ground
  Contact sensors
  Digital pins
