# Fritzing sketch flex (saved by Fritzing 0.9.2b)
breadboards: 1

parts:
  S2 = Round Pushbutton  # not connected
  Teensy_3_1 = Teensy 3.1
  FS1 = Basic Flex Resistor
  R1 = Resistor [tolerance=±20% resistance=10k package="0603 [SMD]"]
  FS2 = Basic Flex Resistor
  R2 = Resistor [tolerance=±20% resistance=10k package="0603 [SMD]"]
  R3 = Resistor [tolerance=±20% resistance=10k package="0603 [SMD]"]
  FS3 = Basic Flex Resistor
  FS4 = Basic Flex Resistor
  FS5 = Basic Flex Resistor
  R4 = Resistor [tolerance=±20% resistance=10k package="0603 [SMD]"]
  R5 = Resistor [tolerance=±20% resistance=10k package="0603 [SMD]"]
  Part1 = IMU Digital Combo Board 6DOF

nets:
  GND: Teensy_3_1.GND, R1.Pin_0, R2.Pin_0, R3.Pin_0, R4.Pin_0, R5.Pin_0, Part1.GND
  N1: Teensy_3_1.A1/D15, R1.Pin_1, FS5.pin_1
  N2: Teensy_3_1.A2/D16, R2.Pin_1, FS4.pin_1
  N3: Teensy_3_1.A3/D17, R3.Pin_1, FS3.pin_1
  N4: Teensy_3_1.A4/D18, Part1.SDA
  N5: Teensy_3_1.A5/D19, Part1.SCL
  N6: Teensy_3_1.A6/D20, FS2.pin_1, R4.Pin_1
  N7: Teensy_3_1.A7/D21, FS1.pin_1, R5.Pin_1
  3V3: Teensy_3_1.3V3, FS1.Pin_2, FS2.Pin_2, FS3.Pin_2, FS4.Pin_2, FS5.Pin_2, Part1.3.3V

notes:
  Analog Pins
  GND
  3.3V
  10k ohm
  Flex Sensors
  6DOF
