# Fritzing sketch voltage_div (saved by Fritzing 0.9.2b)
breadboards: 1

parts:
  U1 = TOUCH [package=touch2]  # not connected
  S2 = Round Pushbutton  # not connected
  Teensy_3_1 = Teensy 3.1
  FS1 = Basic Flex Resistor
  R1 = Resistor [tolerance=±20% resistance=10k package="0603 [SMD]"]

nets:
  N1: Teensy_3_1.GND, R1.Pin_0
  N2: Teensy_3_1.A5/D19, FS1.pin_1, R1.Pin_1
  N3: Teensy_3_1.3V3, FS1.Pin_2

notes:
  A5
  GND
  3.3V
  10k ohm
  Flex Sensor
